// Logisim project Exp2_final.circ as structural Verilog: 1 circuit, main circuit main
module main (
  input  in_1,
  input  in_2,
  input  in_3,
  input  in_4,
  input  in_5,
  input  in_6,
  input  in_7,
  input  in_8,
  input  in_9,
  input  in_10,
  input  in_11,
  input  in_12,
  input  in_13,
  input  in_14,
  input  in_15,
  input  in_16,
  input  in_17,
  input  in_18,
  input  in_19
);

  wire A0, A1, A2, A3, B0, B1, B2, B3, C0, C1, C2, C3, clock_1_out, D0, D1, D2, D3, multiplexer_1_out,
       multiplexer_2_out, multiplexer_3_out, multiplexer_4_out;

  Clock clock_1 (.out(clock_1_out));
  Register #(.width(4)) register_1 (
    .D({in_16, in_12, in_8, in_4}), .en(in_1), .clk(clock_1_out), .Q({D3, D2, D1, D0}));  // open: clr
  Multiplexer #(.enable("true"), .select(2)) multiplexer_1 (
    .in0(A3), .in1(B3), .in2(C3), .in3(D3), .out(multiplexer_1_out), .sel({in_2, in_3}), .en(in_1));
  Register #(.width(4)) register_2 (
    .D({in_17, in_13, in_9, in_5}), .en(in_1), .clk(clock_1_out), .Q({C3, C2, C1, C0}));  // open: clr
  Multiplexer #(.enable("true"), .select(2)) multiplexer_2 (
    .in0(A2), .in1(B2), .in2(C2), .in3(D2), .out(multiplexer_2_out), .sel({in_2, in_3}), .en(in_1));
  Multiplexer #(.enable("true"), .select(2)) multiplexer_3 (
    .in0(A1), .in1(B1), .in2(C1), .in3(D1), .out(multiplexer_3_out), .sel({in_2, in_3}), .en(in_1));
  Register #(.width(4)) register_3 (
    .D({in_18, in_14, in_10, in_6}), .en(in_1), .clk(clock_1_out), .Q({B3, B2, B1, B0}));  // open: clr
  Register #(.width(4)) register_4 (
    .D({in_19, in_15, in_11, in_7}), .en(in_1), .clk(clock_1_out), .Q({A3, A2, A1, A0}));  // open: clr
  // Probe on multiplexer_1_out
  // Probe on multiplexer_2_out
  // Probe on multiplexer_3_out
  // Probe on multiplexer_4_out
  Multiplexer #(.enable("true"), .select(2)) multiplexer_4 (
    .in0(A0), .in1(B0), .in2(C0), .in3(D0), .out(multiplexer_4_out), .sel({in_2, in_3}), .en(in_1));

  // Other names for the same wires on the sheet: A[3:0] = {in_19, in_15, in_11, in_7};
  //   B[3:0] = {in_18, in_14, in_10, in_6}; C[3:0] = {in_17, in_13, in_9, in_5}; D[3:0] = {in_16, in_12, in_8, in_4}
endmodule
