// Logisim project Exp3.4bit.circ as structural Verilog: 1 circuit, main circuit main
module main (
  input  A0,
  input  B0,
  input  C0,
  input  D0,
  input  A1,
  input  B1,
  input  C1,
  input  D1,
  input  A2,
  input  B2,
  input  C2,
  input  D2,
  input  A3,
  input  B3,
  input  C3,
  input  D3,
  input  Enable,
  input  S0,
  input  S1
);

  wire decoder_1_out0, decoder_1_out1, decoder_1_out2, decoder_1_out3;
  wire [3:0] controlled_buffer_1_out;

  Decoder #(.select(2)) decoder_1 (
    .out0(decoder_1_out0), .out1(decoder_1_out1), .out2(decoder_1_out2), .out3(decoder_1_out3),
    .sel({S1, S0}), .en(Enable));
  assign controlled_buffer_1_out[0] = decoder_1_out0 ? A0 : 1'bz;  // Controlled_Buffer controlled_buffer_1
  assign controlled_buffer_1_out[0] = decoder_1_out1 ? A1 : 1'bz;  // Controlled_Buffer controlled_buffer_2
  assign controlled_buffer_1_out[0] = decoder_1_out2 ? A2 : 1'bz;  // Controlled_Buffer controlled_buffer_3
  assign controlled_buffer_1_out[0] = decoder_1_out3 ? A3 : 1'bz;  // Controlled_Buffer controlled_buffer_4
  assign controlled_buffer_1_out[1] = decoder_1_out0 ? B0 : 1'bz;  // Controlled_Buffer controlled_buffer_5
  assign controlled_buffer_1_out[1] = decoder_1_out1 ? B1 : 1'bz;  // Controlled_Buffer controlled_buffer_6
  assign controlled_buffer_1_out[1] = decoder_1_out2 ? B2 : 1'bz;  // Controlled_Buffer controlled_buffer_7
  assign controlled_buffer_1_out[1] = decoder_1_out3 ? B3 : 1'bz;  // Controlled_Buffer controlled_buffer_8
  // Probe on controlled_buffer_1_out
  assign controlled_buffer_1_out[2] = decoder_1_out0 ? C0 : 1'bz;  // Controlled_Buffer controlled_buffer_9
  assign controlled_buffer_1_out[2] = decoder_1_out1 ? C1 : 1'bz;  // Controlled_Buffer controlled_buffer_10
  assign controlled_buffer_1_out[2] = decoder_1_out2 ? C2 : 1'bz;  // Controlled_Buffer controlled_buffer_11
  assign controlled_buffer_1_out[2] = decoder_1_out3 ? C3 : 1'bz;  // Controlled_Buffer controlled_buffer_12
  assign controlled_buffer_1_out[3] = decoder_1_out0 ? D0 : 1'bz;  // Controlled_Buffer controlled_buffer_13
  assign controlled_buffer_1_out[3] = decoder_1_out1 ? D1 : 1'bz;  // Controlled_Buffer controlled_buffer_14
  assign controlled_buffer_1_out[3] = decoder_1_out2 ? D2 : 1'bz;  // Controlled_Buffer controlled_buffer_15
  assign controlled_buffer_1_out[3] = decoder_1_out3 ? D3 : 1'bz;  // Controlled_Buffer controlled_buffer_16
endmodule
