// Logisim project Exp4.circ as structural Verilog: 1 circuit, main circuit main
module main (
  input  A3,
  input  B3,
  input  A2,
  input  B2,
  input  A1,
  input  B1,
  input  A0,
  input  B0,
  input  M
);

  wire adder_1_cout, adder_1_out, adder_2_cout, adder_2_out, adder_3_cout, adder_3_out, adder_4_cout,
       adder_4_out, xor_1_out, xor_2_out, xor_3_out, xor_4_out;

  xor xor_1 (xor_1_out, B3, M);
  // Probe on adder_1_cout
  Adder #(.width(1)) adder_1 (.a(A3), .b(xor_1_out), .out(adder_1_out), .cin(adder_2_cout), .cout(adder_1_cout));
  // Probe on adder_1_out
  xor xor_2 (xor_2_out, B2, M);
  Adder #(.width(1)) adder_2 (.a(A2), .b(xor_2_out), .out(adder_2_out), .cin(adder_3_cout), .cout(adder_2_cout));
  // Probe on adder_2_out
  xor xor_3 (xor_3_out, B1, M);
  Adder #(.width(1)) adder_3 (.a(A1), .b(xor_3_out), .out(adder_3_out), .cin(adder_4_cout), .cout(adder_3_cout));
  // Probe on adder_3_out
  xor xor_4 (xor_4_out, B0, M);
  Adder #(.width(1)) adder_4 (.a(A0), .b(xor_4_out), .out(adder_4_out), .cin(M), .cout(adder_4_cout));
  // Probe on adder_4_out
endmodule
