// Logisim project Exp5.circ as structural Verilog: 1 circuit, main circuit main
module main (
  input  Cin,
  input  S1,
  input  S0,
  input  A0,
  input  B0,
  input  A1,
  input  B1,
  input  A2,
  input  B2,
  input  A3,
  input  B3,
  input  in_12
);

  wire adder_1_cout, adder_2_cout, adder_3_cout, adder_4_cout, multiplexer_1_out, multiplexer_2_out,
       multiplexer_3_out, multiplexer_4_out, not_1_out, not_2_out, not_3_out, not_4_out, not_5_out;
  wire [3:0] adder_1_out;

  Hex_Digit_Display hex_digit_display_1 (.value({A3, A2, A1, A0}));  // open: dp
  Hex_Digit_Display hex_digit_display_2 (.value({B3, B2, B1, B0}));  // open: dp
  not not_1 (not_1_out, B0);
  not not_2 (not_2_out, B1);
  not not_3 (not_3_out, B2);
  not not_4 (not_4_out, B3);
  not not_5 (not_5_out, in_12);
  Multiplexer #(.select(2)) multiplexer_1 (
    .in0(B0), .in1(not_1_out), .in2(not_5_out), .in3(in_12), .out(multiplexer_1_out), .sel({S0, S1}));
  Multiplexer #(.select(2)) multiplexer_2 (
    .in0(B1), .in1(not_2_out), .in2(not_5_out), .in3(in_12), .out(multiplexer_2_out), .sel({S0, S1}));
  Multiplexer #(.select(2)) multiplexer_3 (
    .in0(B2), .in1(not_3_out), .in2(not_5_out), .in3(in_12), .out(multiplexer_3_out), .sel({S0, S1}));
  Multiplexer #(.select(2)) multiplexer_4 (
    .in0(B3), .in1(not_4_out), .in2(not_5_out), .in3(in_12), .out(multiplexer_4_out), .sel({S0, S1}));
  Adder #(.width(1)) adder_1 (.a(A0), .b(multiplexer_1_out), .out(adder_1_out[0]), .cin(Cin), .cout(adder_1_cout));
  Adder #(.width(1)) adder_2 (
    .a(A1), .b(multiplexer_2_out), .out(adder_1_out[1]), .cin(adder_1_cout), .cout(adder_2_cout));
  Adder #(.width(1)) adder_3 (
    .a(A2), .b(multiplexer_3_out), .out(adder_1_out[2]), .cin(adder_2_cout), .cout(adder_3_cout));
  Adder #(.width(1)) adder_4 (
    .a(A3), .b(multiplexer_4_out), .out(adder_1_out[3]), .cin(adder_3_cout), .cout(adder_4_cout));
  // Probe on adder_4_cout
  Hex_Digit_Display hex_digit_display_3 (.value(adder_1_out));  // open: dp
endmodule
