// Logisim project LeftShift.circ as structural Verilog: 1 circuit, main circuit main
module main (
  input  in_1,
  input  in_2
);

  wire clock_1_out, d_ff_1_q, d_ff_2_q, d_ff_3_q, d_ff_4_q;

  Clock clock_1 (.out(clock_1_out));
  // Probe on d_ff_1_q
  D_Flip_Flop d_ff_1 (.clk(clock_1_out), .D(d_ff_2_q), .Q(d_ff_1_q), .reset(in_2));  // open: Qn, preset
  D_Flip_Flop d_ff_2 (.clk(clock_1_out), .D(d_ff_3_q), .Q(d_ff_2_q), .reset(in_2));  // open: Qn, preset
  // Probe on d_ff_2_q
  // Probe on d_ff_3_q
  D_Flip_Flop d_ff_3 (.clk(clock_1_out), .D(d_ff_4_q), .Q(d_ff_3_q), .reset(in_2));  // open: Qn, preset
  // Probe on d_ff_4_q
  D_Flip_Flop d_ff_4 (.clk(clock_1_out), .D(in_1), .Q(d_ff_4_q), .reset(in_2));  // open: Qn, preset
endmodule
